# Fritzing sketch RRFTracker_multiplex (saved by Fritzing 0.9.2b)
breadboards: 2

parts:
  OLED_I2C1 = OLED 128x64 I2C Monochrome Display  # not connected
  Composant1 = Adafruit TCA9548A
  OLED_I2C2 = OLED 128x64 I2C Monochrome Display  # not connected
  OLED_I2C3 = OLED 128x64 I2C Monochrome Display  # not connected
  OLED_I2C4 = OLED 128x64 I2C Monochrome Display  # not connected
  OLED_I2C5 = OLED 128x64 I2C Monochrome Display  # not connected
  Composant2 = node32s
  R1 = Resistor [tolerance=±5% resistance=330 package="2010 [SMD]"]
  R2 = Resistor [tolerance=±5% resistance=330 package="2010 [SMD]"]
  R3 = Resistor [tolerance=±5% resistance=330 package="2010 [SMD]"]
  LED1 = LED - 3mm [color="Green (570nm)" package="3 mm [THT]"]  # not connected
  LED2 = LED - 3mm [color="Red (635nm)" package="3 mm [THT]"]  # not connected
  LED3 = LED - 3mm [color="Blue (470nm)" package="3 mm [THT]"]  # not connected

nets:
  VCC: Composant1.VCC, Composant2.5V
  GND: Composant1.GND, Composant2.GND, R1.Pin_1, R2.Pin_1, R3.Pin_1
  N1: Composant1.INPUTSDA, Composant2.IO21
  N2: Composant1.INPUTSCL, Composant2.IO23

custom parts:
  Adafruit TCA9548A: You just found the perfect I2C sensor, and you want to wire up two or three or more of them to your Arduino when you realize "Uh oh, this chip has a fixed I2C address, and from what I know about I2C, you cannot have two devices with the same address on the same SDA/SCL pins!" Are you out of luck? You would be, if you didn't have this ultra-cool TCA9548A 1-to-8 I2C multiplexer! Finally, a way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
